# Fritzing sketch fritzingGPIOSchematic (saved by Fritzing 0.9.3b)

parts:
  S1 = PH meter [package=THT]
  M1 = >Wemos D1 R32  # not connected
  Mod2 = Arduino Sensor Shield v5.0
  Part1 = Solid State High Level Relay Module [package=relay]
  S3 = PH meter [package=THT]
  R11 = Resistor [tolerance=±5% resistance=4.7k package="2512 [SMD]"]
  LM35_TempSensor1 = LM35 TempSensor
  Part2 = Solid State High Level Relay Module [package=relay]
  Part3 = Solid State High Level Relay Module [package=relay]
  Part4 = Solid State High Level Relay Module [package=relay]
  LCD4 = LCD screen
  LCM1602_IIC3 = LCM1602 IIC [part_number="LCM1602 IIC" chip_label="LCM1602 IIC" package="DIP (Dual Inline) [THT]"]
  Part5 = US-100 Ultrasonic Rangefinder
  AM1 = AM2302 Humidity and Temperature Sensor
  S22 = Round Pushbutton
  S23 = Round Pushbutton
  S24 = Round Pushbutton
  S25 = Round Pushbutton

nets:
  N1: S1.pin1, Mod2.A4-SIG
  VCC: S1.pin2, Mod2.A4-VCC, Mod2.A5-VCC, Mod2.AREF-V, Mod2.13-V, Mod2.7-V, Mod2.4-V, Mod2.0-V, Part1.DC+, S3.pin2, R11.Pin_1, LM35_TempSensor1.POWER, LCM1602_IIC3.VCC, Part5.VCC, AM1.VDD
  GND: S1.pin3, Mod2.A1-GND, Mod2.A4-GND, Mod2.A5-GND, Mod2.IIC-GND, Mod2.AREF-G, Mod2.13-G, Mod2.9-G, Mod2.8-G, Mod2.7-G, Mod2.6-G, Mod2.5-G, Mod2.4-G, Mod2.0-G, Part1.DC-, S3.pin3, LM35_TempSensor1.GND, LCM1602_IIC3.GND, Part5.GND, AM1.GND, S22.leg1, S23.leg0, S24.leg0, S25.leg0
  N2: Mod2.SD-D11, Mod2.11-S, Part3.CH1
  N3: Mod2.SD-D13, Mod2.13-S, Part1.CH1
  N4: Mod2.SD-D12, Mod2.12-S, Part2.CH1
  N5: Mod2.A1-SIG, Part5.Trig/Tx
  N6: Mod2.A2-SIG, Part5.Echo/Rx
  N7: Mod2.A5-SIG, S3.pin1
  N8: Mod2.10-S, Mod2.ParallelLCD-D10, Part4.CH1
  N9: Mod2.9-S, Mod2.ParallelLCD-D9, S22.leg0
  N10: Mod2.8-S, Mod2.ParallelLCD-D8, S25.leg1
  N11: Mod2.6-S, Mod2.ParallelLCD-D6, S24.leg1
  N12: Mod2.5-S, Mod2.ParallelLCD-D5, S23.leg1
  N13: Mod2.4-S, Mod2.SerialLCD-D4, AM1.DATA
  N14: Mod2.3-S, LCM1602_IIC3.SDA
  N15: Mod2.2-S, Mod2.SerialLCD-D2, LCM1602_IIC3.SCL
  N16: R11.Pin_0, LM35_TempSensor1.INPUT
  VSS: LCD4.VSS, LCM1602_IIC3.VSS
  VDD: LCD4.VDD, LCM1602_IIC3.VDD
  N17: LCD4.V0, LCM1602_IIC3.V0
  N18: LCD4.RS, LCM1602_IIC3.RS
  N19: LCD4.R/W, LCM1602_IIC3.RW
  N20: LCD4.E, LCM1602_IIC3.E
  N21: LCD4.DB0, LCM1602_IIC3.D0
  N22: LCD4.DB1, LCM1602_IIC3.D1
  N23: LCD4.DB2, LCM1602_IIC3.D2
  N24: LCD4.DB3, LCM1602_IIC3.D3
  N25: LCD4.DB4, LCM1602_IIC3.D4
  N26: LCD4.DB5, LCM1602_IIC3.D5
  N27: LCD4.DB6, LCM1602_IIC3.D6
  N28: LCD4.DB7, LCM1602_IIC3.D7
  N29: LCD4.LED+, LCM1602_IIC3.A
  N30: LCD4.LED-, LCM1602_IIC3.K

notes:
  Relay 1
  Relay 2
  Relay 3
  Relay 4
  sensor temperatur air
  TDS Sensor
  PH Sensor
  Sensor Jarak
  Trigger (blue wire)
  Echo (Yellow wire)
  Sensor temperatur dan kelembapan ruangan
  Button Merah
  (D9)
  Button
  Hitam
  (D5)
  Button Kuning
  (D6)
  Button Hijau
  (D8)

custom parts:
  >Wemos D1 R32: Wemos D1 R32 - This board is used with dual-mode Wi-Fi and Bluetooth chips, which is safe, reliable, and scalable to a variety of applications. DC in 5V-12V, 1 analog input(3.2V max input), a Micro USB connection, Compatible with D1 R32=WiFi+bluetooth+UNO
  Arduino Sensor Shield v5.0: Arduino Sensor Shield v5.0 provides I2C interface, Bluetooth module communication interface, SD card module communication interface, APC220 wireless RF modules communication interface, RB URF V1.1 ultrasonic sensors interface, 12864 LCD serial and parallel interface, 32 servo controller interfaces. In addition (with the sel jumper removed) allows an external power supply for the servos as the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
  Solid State High Level Relay Module: 5V Omron solid state relay 240V 2A output with resistance fuse.
  LCM1602 IIC: I2C-Module to use a 1602 or 2004 LCD on with the wire.h libory Serial LCD Modul
